# Fritzing sketch ispindel-v150-ESP12F--SMD1206 (saved by Fritzing 0.9.3b)
circuit board: 6cm x 2.6cm
breadboards: 1

parts:
  ESP-12F = ESP8266 WiFi Module [part_number=ESP8266]
  R6 = Resistor [tolerance=±5% resistance=4.7k package="1206 [SMD]"]
  R5 = Resistor [tolerance=±5% resistance=10k package="1206 [SMD]"]
  R4 = Resistor [tolerance=±5% resistance=10k package="1206 [SMD]"]
  R3 = Resistor [tolerance=±5% resistance=220k package="1206 [SMD]"]
  R2 = Resistor [tolerance=±5% resistance=10k package="1206 [SMD]"]
  R1 = Resistor [tolerance=±5% resistance=470 package="1206 [SMD]"]
  S1 = SPST Switch [package=switch-spdt_lock.007s]
  J1 = male pin header, 2 pins [form="♂ (male)"]
  GY-521 = female pin header, 4 pins [form="♀ (female)" part_number=GY-521]
  PROG = SWITCH-MOMENTARY-2 [package=tactile-switch-1101ne]
  RESE = SWITCH-MOMENTARY-2 [package=tactile-switch-1101ne]
  TP4056 = TP4056 [chip_label=TP4056 package="DIP (Dual Inline) [THT]"]
  DS1 = DS18B20 1-Wire Temperature Sensor [part_number=DS18B20]

nets:
  N1: ESP-12F.RXD, J1.pin1
  VCC: ESP-12F.VCC, R6.Pin_1, R5.Pin_0, R4.Pin_0, R3.Pin_0, S1.S, GY-521.pin1, DS1.VDD
  N2: ESP-12F.GPIO_0, PROG.1
  N3: ESP-12F.GPIO_2, R5.Pin_1
  N4: ESP-12F.EN, R4.Pin_1
  GND: ESP-12F.GND, R2.Pin_0, GY-521.pin2, PROG.2, RESE.2, TP4056.pin6, DS1.GND
  N5: ESP-12F.TXD, J1.pin2
  N6: ESP-12F.GPIO_15, R2.Pin_1
  N7: ESP-12F.GPIO_4, GY-521.pin4
  N8: ESP-12F.GPIO_5, GY-521.pin3
  N9: ESP-12F.ADC_0, R3.Pin_1
  N10: ESP-12F.GPIO_16, R1.Pin_0
  N11: ESP-12F.GPIO_14, R6.Pin_0, DS1.DQ
  N12: ESP-12F.REST, R1.Pin_1, RESE.1
  N13: S1.P, TP4056.pin3

notes:
  Knocker Brewery
  iSpindel v1.5

custom parts:
  ESP8266 WiFi Module: Generic WiFi Module based on the ESP8266 with onboard PCB antenna and UART communications
  TP4056: A DIP stand-in part for whatever IC you want. With 6 pins on a 300mil dual inline package (DIP) footprint.
