# Fritzing sketch ispindel-v150-WemosD1--SMD1206 (saved by Fritzing 0.9.3b)
circuit board: 12cm x 2.56875cm
breadboards: 1

parts:
  WeMos_D1_Mini1 = WeMos D1 Mini
  TP4056 = TP4056 [chip_label=TP4056 package="DIP (Dual Inline) [THT]"]
  U1 = SPST Switch [package=switch-spdt]
  DS1 = DS18B20 1-Wire Temperature Sensor [part_number=DS18B20]
  GY521 = MPU-6050 Board GY-521 [form="♀ (female)" package=THT]
  220kΩ = Resistor [tolerance=±5% resistance=220k package="1206 [SMD]"]
  4_7kΩ = Resistor [tolerance=±5% resistance=4.7k package="1206 [SMD]"]
  470Ω = Resistor [tolerance=±5% resistance=470 package="1206 [SMD]"]

nets:
  5V: WeMos_D1_Mini1.5V, U1.O, DS1.VDD, GY521.pin1, 220kΩ.Pin_0, 4_7kΩ.Pin_1
  N1: WeMos_D1_Mini1.A0, 220kΩ.Pin_1
  N2: WeMos_D1_Mini1.D0, 470Ω.Pin_0
  N3: WeMos_D1_Mini1.D3, GY521.pin4
  N4: WeMos_D1_Mini1.D4, GY521.pin3
  N5: WeMos_D1_Mini1.D6, DS1.DQ, 4_7kΩ.Pin_0
  N6: WeMos_D1_Mini1.G, TP4056.pin6, DS1.GND, GY521.pin2
  N7: WeMos_D1_Mini1.RST, 470Ω.Pin_1
  N8: TP4056.pin3, U1.P

notes:
  Knocker Brewery iSpindle v1.5 SMD

custom parts:
  TP4056: A DIP stand-in part for whatever IC you want. With 6 pins on a 300mil dual inline package (DIP) footprint.
  MPU-6050 Board GY-521: Acelerometro y Giroscopio MPU-6050 Board GY-521
